// Logisim project circuit.circ as structural Verilog
module full_adder (
  input  in_1,
  input  in_2,
  input  in_3,
  input  in_4,
  input  in_5,
  input  in_6,
  input  in_7,
  input  in_8,
  output out_9,
  output out_10,
  output out_11,
  output out_12,
  output out_13
);

  wire and_1_out, and_2_out, and_3_out, and_4_out, and_5_out, and_6_out, and_7_out, or_1_out, or_2_out,
       xor_2_out, xor_3_out, xor_4_out;

  xor xor_1 (out_9, in_1, in_2);
  and and_1 (and_1_out, in_1, in_2);
  xor xor_2 (xor_2_out, in_3, in_4);
  and and_2 (and_2_out, in_3, in_4);
  xor xor_3 (xor_3_out, in_5, in_6);
  and and_3 (and_3_out, in_5, in_6);
  xor xor_4 (xor_4_out, in_7, in_8);
  and and_4 (and_4_out, in_7, in_8);
  and and_5 (and_5_out, xor_2_out, and_1_out);
  xor xor_5 (out_10, xor_2_out, and_1_out);
  xor xor_6 (out_11, xor_3_out, or_1_out);
  and and_6 (and_6_out, xor_3_out, or_1_out);
  xor xor_7 (out_12, xor_4_out, or_2_out);
  and and_7 (and_7_out, xor_4_out, or_2_out);
  or or_1 (or_1_out, and_5_out, and_2_out);
  or or_2 (or_2_out, and_6_out, and_3_out);
  or or_3 (out_13, and_7_out, and_4_out);

  // Notes on the sheet:
  //   in_1: pull=up
  //   in_2: pull=up
  //   adder
endmodule

module ALU (
  input  in_1,
  input  in_2,
  input  in_3,
  input  in_4,
  input  in_5,
  input  in_6,
  input  in_7,
  input  in_8,
  input  in_9,
  input  in_10,
  input  in_11,
  input  in_12,
  input  in_13,
  input  in_14,
  input  in_15,
  input  in_16,
  input  in_17,
  input  in_18,
  input  in_19,
  input  in_20,
  input  in_21,
  input  in_22,
  input  in_23,
  input  in_24,
  input  in_25,
  input  in_26,
  input  in_27,
  input  in_28,
  input  in_29,
  input  in_30,
  input  in_31,
  input  in_32,
  input  in_33,
  input  in_34,
  input  in_35,
  input  in_36,
  input  in_37,
  input  in_38,
  input  s0,
  input  in_40,
  input  s1,
  input  s2
);

  wire [2:1] undriven_3;
  wire [7:0] and_1_p9, and_1_p10, and_1_p11, full_adder_1_p9, full_adder_1_p10, full_adder_1_p11,
       full_adder_1_p12, full_adder_1_p13, multiplexer_3_out, or_1_p9, or_1_p10, or_1_p11, or_1_p12,
       right_shifter_1_p3, right_shifter_1_p5, right_shifter_1_p7, right_shifter_1_p10, subtractor_1_p9,
       subtractor_1_p11, subtractor_1_p12, subtractor_1_p13;
  wire [7:1] undriven, undriven_2, undriven_4;

  // full_adder full_adder_1: pin names not known; wires that end beside it: in_1, in_4, in_8, in_12, in_14, in_17, in_20, in_23, full_adder_1_p9, full_adder_1_p10, full_adder_1_p11, full_adder_1_p12, full_adder_1_p13
  // subtractor subtractor_1: pin names not known; wires that end beside it: in_25, in_30, in_31, in_33, in_35, in_37, in_38, in_40, subtractor_1_p9, full_adder_1_p10, subtractor_1_p11, subtractor_1_p12, subtractor_1_p13
  // and and_1: pin names not known; wires that end beside it: in_2, in_5, in_7, in_9, in_11, in_15, in_18, in_22, and_1_p9, and_1_p10, and_1_p11, subtractor_1_p12
  // right_shifter right_shifter_1: pin names not known; wires that end beside it: in_32, in_36, right_shifter_1_p3, in_26, right_shifter_1_p5, in_27, right_shifter_1_p7, in_28, in_29, right_shifter_1_p10, in_34
  // OR or_1: pin names not known; wires that end beside it: in_3, in_6, in_10, in_13, in_16, in_19, in_21, in_24, or_1_p9, or_1_p10, or_1_p11, or_1_p12
  Multiplexer #(.select(3), .width(8), .enable("false")) multiplexer_1 (
    .in0(full_adder_1_p9), .in1(subtractor_1_p9), .in2(and_1_p9), .in3(or_1_p9), .in4(right_shifter_1_p10),
    .sel({undriven_3, s0}));  // open: in5, in6, in7, out
  Multiplexer #(.select(3), .width(8), .disabled(0), .enable("false")) multiplexer_2 (
    .in0(full_adder_1_p10), .in1(full_adder_1_p10), .in2(and_1_p10), .in3(or_1_p10),
    .in4(right_shifter_1_p7), .sel({undriven_3, s0}));  // open: in5, in6, in7, out
  Multiplexer #(.select(3), .width(8), .enable("false")) multiplexer_3 (
    .in0(full_adder_1_p11), .in1(subtractor_1_p11), .in2(and_1_p11), .in3(or_1_p11),
    .in4(right_shifter_1_p5), .out(multiplexer_3_out), .sel({undriven_3, s0}));  // open: in5, in6, in7
  Multiplexer #(.select(3), .width(8), .disabled(0), .enable("false")) multiplexer_4 (
    .in0(full_adder_1_p12), .in3(subtractor_1_p12), .in4(subtractor_1_p12), .in5(or_1_p12),
    .in6(right_shifter_1_p3), .sel({undriven_3, s0}));  // open: in1, in2, in7, out
  Multiplexer #(.select(3), .width(8), .enable("false")) multiplexer_5 (
    .in0(full_adder_1_p13), .in1(subtractor_1_p13), .in2({undriven, 1'b0}), .in3({undriven_4, 1'b0}),
    .in5({undriven_2, 1'b0}), .sel({undriven_3, s0}));  // open: in4, in6, in7, out
  // Pins of 1 and 8 bits meet at {undriven_2, 1'b0}
  // Pins of 1 and 8 bits meet at {undriven, 1'b0}
  // Pins of 1 and 3 bits meet at {undriven_3, s0}
  // Pins of 1 and 8 bits meet at {undriven_4, 1'b0}

  assign s1 = s0;
  assign s2 = s0;
endmodule

module \and  (
  input  in_1,
  input  in_2,
  input  in_3,
  input  in_4,
  input  in_5,
  input  in_6,
  input  in_7,
  input  in_8,
  output out_9,
  output out_10,
  output out_11,
  output out_12
);

  and and_1 (out_9, in_1, in_2);
  and and_2 (out_10, in_3, in_4);
  and and_3 (out_11, in_5, in_6);
  and and_4 (out_12, in_7, in_8);

  // Notes on the sheet:
  //   in_1: pull=up
endmodule

module OR (
  input  in_1,
  input  in_2,
  input  in_3,
  input  in_4,
  input  in_5,
  input  in_6,
  input  in_7,
  input  in_8,
  output out_9,
  output out_10,
  output out_11,
  output out_12
);

  or or_1 (out_9, in_1, in_2);
  or or_2 (out_10, in_3, in_4);
  or or_3 (out_11, in_5, in_6);
  or or_4 (out_12, in_7, in_8);
endmodule

module subtractor (
  input  in_1,
  input  in_2,
  input  in_3,
  input  in_4,
  input  in_5,
  input  in_6,
  input  in_7,
  input  in_8,
  output out_9,
  output out_10,
  output out_11,
  output out_12,
  output out_13
);

  wire and_1_out, and_2_out, and_3_out, and_4_out, and_5_out, and_6_out, and_7_out, not_1_out, not_2_out,
       not_3_out, not_4_out, or_1_out, or_2_out, xor_2_out, xor_3_out, xor_4_out;

  not not_1 (not_1_out, in_2);
  not not_2 (not_2_out, in_4);
  not not_3 (not_3_out, in_8);
  not not_4 (not_4_out, in_6);
  xor xor_1 (out_9, in_1, not_1_out);
  and and_1 (and_1_out, in_1, not_1_out);
  xor xor_2 (xor_2_out, in_3, not_2_out);
  and and_2 (and_2_out, in_3, not_2_out);
  xor xor_3 (xor_3_out, in_5, not_4_out);
  and and_3 (and_3_out, in_5, not_4_out);
  xor xor_4 (xor_4_out, in_7, not_3_out);
  and and_4 (and_4_out, in_7, not_3_out);
  and and_5 (and_5_out, xor_2_out, and_1_out);
  xor xor_5 (out_10, xor_2_out, and_1_out);
  xor xor_6 (out_11, xor_3_out, or_1_out);
  and and_6 (and_6_out, xor_3_out, or_1_out);
  xor xor_7 (out_12, xor_4_out, or_2_out);
  and and_7 (and_7_out, xor_4_out, or_2_out);
  or or_1 (or_1_out, and_5_out, and_2_out);
  or or_2 (or_2_out, and_6_out, and_3_out);
  or or_3 (out_13, and_7_out, and_4_out);

  // Notes on the sheet:
  //   in_1: pull=up
  //   subtractor 
endmodule

module right_shifter (
  input  in_1,
  input  in_2,
  input  in_3,
  input  in_4,
  input  in_5,
  input  in_6,
  input  in_7,
  output out_8,
  output out_9,
  output out_10,
  output out_11
);

  wire and_1_out, and_2_out, and_3_out, and_4_out, and_5_out, and_6_out, and_7_out, and_8_out, and_9_out,
       and_10_out, and_11_out, not_1_out, not_2_out, not_3_out, not_4_out, not_5_out, or_1_out;

  not not_1 (not_1_out, in_5);
  and and_1 (and_1_out, not_1_out, in_7);
  and and_2 (and_2_out, in_5, in_4);
  and and_3 (and_3_out, and_1_out, in_1);
  or or_1 (or_1_out, and_2_out, and_3_out);
  and and_4 (and_4_out, or_1_out, in_6);
  or or_2 (out_10, and_4_out, and_5_out);
  not not_2 (not_2_out, in_6);
  and and_5 (and_5_out, in_1, not_2_out);
  and and_6 (and_6_out, in_1, in_6);
  not not_3 (not_3_out, in_6);
  and and_7 (and_7_out, in_2, not_3_out);
  or or_3 (out_11, and_6_out, and_7_out);
  and and_8 (and_8_out, in_2, in_6);
  and and_9 (and_9_out, in_3, not_4_out);
  or or_4 (out_8, and_8_out, and_9_out);
  not not_4 (not_4_out, in_6);
  and and_10 (and_10_out, in_3, in_6);
  and and_11 (and_11_out, in_4, not_5_out);
  or or_5 (out_9, and_10_out, and_11_out);
  not not_5 (not_5_out, in_6);

  // Notes on the sheet:
  //   right arithmetic shifter 
endmodule
